// Logisim project LC-3-v1.circ as structural Verilog: 18 circuits, main circuit main
// RES
module main (
  input  IR,
  input  Reset,
  output out_3,
  output out_4,
  output out_5,
  output out_6,
  output out_7,
  output out_8,
  output out_9,
  output out_10,
  output [15:0] out_11,
  output [15:0] out_12,
  output [15:0] out_13,
  output [15:0] out_14,
  output [15:0] out_15,
  output [15:0] out_16,
  output [15:0] out_17,
  output [15:0] out_18,
  output [15:0] out_19,
  output halt,
  output [15:0] out_21,
  output [15:0] out_22,
  output [15:0] out_23,
  output [15:0] out_24
);

  wire decodeir_1_writereg, getcst_1_usecst, or16_1_out_2, or16_2_out_2, ramctrl_1_memload,
       ramctrl_1_memstore;
  wire [2:0] choixdrsr_jsr_1_output, nzp_1_nzp;
  wire [15:0] alu_1_output, getcst_1_cst, RegIN, registres_1_out_sr1, registres_1_out_sr2;

  BiClock biclock_1 (.reset(Reset), .signal0(out_4), .signal1(out_5));
  RegPC regpc_1 (
    .H(out_5), .PC(out_11), .Reset(Reset), .IR(out_12), .R(registres_1_out_sr1), .TestNZP(out_7), .Jump(out_6));
  // Probe on out_11
  // Probe on out_13
  GetAddr getaddr_1 (.PC(out_11), .BaseR(registres_1_out_sr1), .IR(out_12), .Addr(out_13), .Fetch(out_4));
  // Probe on out_14
  LED led_1 (.in(out_8));
  RamCtrl ramctrl_1 (
    .Store(out_9), .Fetch(out_4), .Exec(out_5), .Load(out_8), .MemStore(ramctrl_1_memstore),
    .MemLoad(ramctrl_1_memload));
  LED led_2 (.in(out_9));
  // Probe on out_15
  RAM #(.addrWidth(16), .dataWidth(16), .bus("separate")) ram_1 (
    .addr(out_13), .din(out_14), .data(out_15), .str(ramctrl_1_memstore), .clk(ramctrl_1_memstore),
    .ld(ramctrl_1_memload));  // open: sel, clr
  Register #(.width(16), .trigger("falling")) RegIR (.D(out_15), .Q(out_12), .clk(out_4));  // open: en, clr
  DecodeIR decodeir_1 (.IR(out_12), .WriteReg(decodeir_1_writereg), .Jump(out_6), .Load(out_8), .Store(out_9));
  // Probe on choixdrsr_jsr_1_output
  // Probe on out_12[8:6]
  // Probe on out_12[2:0]
  choixDRSR_JSR choixdrsr_jsr_1 (.IR(out_12), .Output(choixdrsr_jsr_1_output));
  // Probe on getcst_1_cst
  GetCst getcst_1 (.IR(out_12), .Cst(getcst_1_cst), .UseCst(getcst_1_usecst));
  // Probe on out_12[15:14]
  and and_1 (out_10, decodeir_1_writereg, out_5);
  Registres registres_1 (
    .SR1(out_12[8:6]), .IN(RegIN), .SR2(out_12[2:0]), .WriteReg(out_10), .DR_SR(choixdrsr_jsr_1_output),
    .OUT_SR1(registres_1_out_sr1), .OUT_SR2(registres_1_out_sr2), .OUT_SR(out_14), .R0(out_16), .R1(out_17),
    .R2(out_18), .R3(out_19), .R4(out_21), .R5(out_22), .R6(out_23), .R7(out_24));
  // Probe on registres_1_out_sr1
  ALU alu_1 (
    .UseCst(getcst_1_usecst), .e2(out_12[15:14]), .Input1(registres_1_out_sr1), .Input2(registres_1_out_sr2),
    .Cst(getcst_1_cst), .Output(alu_1_output));
  // Probe on registres_1_out_sr2
  // Probe on alu_1_output
  NZP nzp_1 (.RES(RegIN), .NZP(nzp_1_nzp), .WriteReg(out_10), .IR(out_12), .TestNZP(out_7));
  // Probe on nzp_1_nzp
  Or16 or16_1 (.in_1(out_12), .out_2(or16_1_out_2));
  Or16 or16_2 (.in_1(out_11), .out_2(or16_2_out_2));
  // Probe on out_16
  // Probe on out_17
  // Probe on out_18
  // Probe on out_19
  // Probe on out_21
  // Probe on out_22
  // Probe on out_23
  // Probe on out_24
  and and_2 (halt, ~or16_1_out_2, or16_2_out_2);  // AND_Gate
  WriteVal writeval_1 (.Load(out_8), .ALURes(alu_1_output), .MemOUT(out_15), .IR(out_12), .PC(out_11), .RegIN(RegIN));

  assign out_3 = IR;

  // Other names for the same wires on the sheet: Addr[15:0] = out_13; Condition = out_7; Exec = out_5; Fetch = out_4;
  //   IR_t[15:0] = out_12; JumpInstr = out_6; Load = out_8; MemIN[15:0] = out_14; MemOUT[15:0] = out_15;
  //   PC[15:0] = out_11; R0[15:0] = out_16; R1[15:0] = out_17; R2[15:0] = out_18; R3[15:0] = out_19;
  //   R4[15:0] = out_21; R5[15:0] = out_22; R6[15:0] = out_23; R7[15:0] = out_24; Store = out_9; test = IR;
  //   WriteReg = out_10

  // Notes on the sheet:
  //   R
  //   IR
  //   R
  //   IR
  //   RAM
  //   Traces (NE PAS MODIFIER)______________________________________________________________________________________________________
  //   GetOp
  //   Arret des traces au 1er NOP
endmodule

module ALU (
  input  [15:0] Input1,
  input  [15:0] Input2,
  input  [15:0] Cst,
  input  UseCst,
  input  [1:0] e2,
  output [15:0] Output
);

  wire [15:0] adder_1_out, and_1_out, multiplexer_1_out, not_1_out, scan_2_1_out_3;

  Multiplexer #(.width(16), .enable("false")) multiplexer_1 (
    .in0(Input2), .in1(Cst), .out(multiplexer_1_out), .sel(UseCst));
  Adder #(.width(16)) adder_1 (.a(multiplexer_1_out), .b(Input1), .out(adder_1_out));  // open: cin, cout
  assign and_1_out = Input1 & multiplexer_1_out;  // AND_Gate and_1, 16 bits wide
  Multiplexer #(.select(2), .width(16), .enable("false")) multiplexer_2 (
    .in0(adder_1_out), .in1(and_1_out), .in2(not_1_out), .in3(scan_2_1_out_3), .out(Output), .sel(e2));
  assign not_1_out = ~Input1;  // NOT_Gate not_1, 16 bits wide
  Scan_2 scan_2_1 (.IR_2(multiplexer_1_out), .out_3(scan_2_1_out_3), .IR(Input1));

  // Notes on the sheet:
  //   c'est le circuit SCAN-2 qui est brancher 
  //   A COMPLETER v1
endmodule

module BiClock (
  input  reset,
  output signal0,
  output signal1
);

  wire and_1_out, horloge_out, not_1_out, register_1_q;

  Clock horloge (.out(horloge_out));
  not not_1 (not_1_out, register_1_q);
  Register #(.width(1), .trigger("falling")) register_1 (
    .D(not_1_out), .Q(register_1_q), .clk(horloge_out), .clr(reset));  // open: en
  and and_1 (and_1_out, horloge_out, ~reset);  // AND_Gate
  and and_2 (signal0, ~register_1_q, and_1_out);  // AND_Gate
  and and_3 (signal1, register_1_q, and_1_out);

  // Notes on the sheet:
  //   Ce module divise une horloge en deux sous-horloges alternées
  //   Chronogrammes :
  //   horloge: 0101010101 signal0: 0100010001 signal1: 000100010
  //   registre 1-bit
  //   Enable
  //   select : 0 / 1
endmodule

module DecodeIR (
  input  [15:0] IR,
  output Store,
  output Load,
  output Jump,
  output WriteReg
);

  wire and_1_out, and_2_out, and_3_out, decoder_1_out1, not_1_out, not_2_out, not_3_out, xor_1_out;

  Decoder #(.select(2), .enable("false")) decoder_1 (
    .out0(Jump), .out1(decoder_1_out1), .out2(Load), .out3(Store), .sel(IR[13:12]));
  // Probe on decoder_1_out1
  not not_1 (not_1_out, IR[12]);
  not not_2 (not_2_out, IR[13]);
  not not_3 (not_3_out, IR[15]);
  and and_1 (and_1_out, not_1_out, not_2_out);
  and and_2 (and_2_out, IR[14], not_3_out);
  xor xor_1 (xor_1_out, IR[12], IR[13]);
  and and_3 (and_3_out, and_1_out, and_2_out);
  or or_1 (WriteReg, xor_1_out, and_3_out);

  // Notes on the sheet:
  //   Types d'instructions
  //   Instruction modifiant les registres ?
  //   On regarde les bits 12 et 13, et avec le décodeur, on sélectionne l'opération :
  //   00 - sauts, 01 - arithmétiques et logiques, 11 - rengement, 10 - chargement
  //   pour savoir si WriteReg est actif on regarde si un des deux bit 12 ou 13 est activé
  //   ce qui correspond aux load ou aux operation arithmétique
  //   et pour le cas de JSR on check tous l'OPCODE
endmodule

module GetAddr (
  input  [15:0] IR,
  input  Fetch,
  input  [15:0] PC,
  input  [15:0] BaseR,
  output [15:0] Addr
);

  wire or_1_out;
  wire [15:0] adder_1_out, adder_2_out, multiplexer_1_out, offset6_1_off6, offset9_1_off9;

  Offset9 offset9_1 (.IR(IR), .Off9(offset9_1_off9));
  Offset6 offset6_1 (.IR(IR), .Off6(offset6_1_off6));
  Adder #(.width(16)) adder_1 (.a(offset6_1_off6), .b(BaseR), .out(adder_1_out));  // open: cin, cout
  Adder #(.width(16)) adder_2 (.a(offset9_1_off9), .b(PC), .out(adder_2_out), .cin(1'b1));  // open: cout
  Multiplexer #(.width(16), .disabled(0), .enable("false")) multiplexer_1 (
    .in0(adder_2_out), .in1(adder_1_out), .out(multiplexer_1_out), .sel(IR[14]));
  or or_1 (or_1_out, ~IR[13], Fetch);  // OR_Gate
  Multiplexer #(.width(16), .disabled(0), .enable("false")) multiplexer_2 (
    .in0(multiplexer_1_out), .in1(PC), .out(Addr), .sel(or_1_out));

  // Notes on the sheet:
  //   PC+SEXT(Offset6)
  //   b14: label or BaseR?
  //   PC+SEXT(Offset9)
  //   b13: Load ou Store?
  //   Pourquoi ?
endmodule

module GetCst (
  input  [15:0] IR,
  output [15:0] Cst,
  output UseCst
);

  assign Cst = {{11{IR[4]}}, IR[4:0]};  // Bit_Extender bit_extender_1

  assign UseCst = IR[5];
endmodule

module NZP (
  input  [15:0] RES,
  input  WriteReg,
  input  [15:0] IR,
  output [2:0] NZP,
  output TestNZP
);

  wire and_1_out, and_2_out, and_3_out;
  wire [2:0] comparator_1_gt, register_1_q;

  Comparator #(.width(16)) comparator_1 (
    .a(RES), .b({16{1'b0}}), .gt(comparator_1_gt[0]), .eq(comparator_1_gt[1]), .lt(comparator_1_gt[2]));
  Register #(.width(3), .trigger("falling")) register_1 (.D(NZP), .Q(register_1_q), .clk(WriteReg));  // open: en, clr
  Multiplexer #(.width(3)) multiplexer_1 (
    .in0(register_1_q), .in1(comparator_1_gt), .out(NZP), .sel(WriteReg));  // open: en
  and and_1 (and_1_out, NZP[0], IR[9]);
  and and_2 (and_2_out, NZP[1], IR[10]);
  and and_3 (and_3_out, NZP[2], IR[11]);
  or or_1 (TestNZP, and_1_out, and_2_out, and_3_out);

  // Notes on the sheet:
  //   Entrées non utilisées pour l'instant
  //   (Resultat du calcul courant)
  //   si 1, instruction doit actualiser NZP
  //   (Instruction courante)
  //   On compare la valeur du résultat à 0.
  //   On vérifie les bits 9-11 qui déterminent la condition de saut
  //   Si l'un des bits correspond à la valeur NSP, TestNZP change à 1
  //   Si WriteReg est 1, on actualise NZP, sinon, on garde le valeur sans changer NZP
  //   Valeur actuelle du registre d'état NZP
  //   Test de saut : vrai siau moins un flag est vrai
endmodule

// Off6
module Offset6 (
  input  [15:0] IR,
  output [15:0] Off6
);

  assign Off6 = {{10{IR[5]}}, IR[5:0]};  // Bit_Extender bit_extender_1
endmodule

// Off9
module Offset9 (
  input  [15:0] IR,
  output [15:0] Off9
);

  assign Off9 = {{7{IR[8]}}, IR[8:0]};  // Bit_Extender bit_extender_1
endmodule

module Or16 (
  input  [15:0] in_1,
  output out_2
);

  wire [1:0] or_2_out;
  wire [7:0] or_1_out;

  assign or_1_out = in_1[7:0] | in_1[15:8];  // OR_Gate or_1, 8 bits wide
  assign or_2_out = or_1_out[1:0] | or_1_out[3:2] | or_1_out[5:4] | or_1_out[7:6];  // OR_Gate or_2, 2 bits wide
  or or_3 (out_2, or_2_out[0], or_2_out[1]);
endmodule

module RamCtrl (
  input  Exec,
  input  Fetch,
  input  Load,
  input  Store,
  output MemLoad,
  output MemStore
);

  wire and_1_out;

  and and_1 (and_1_out, Exec, Load);
  and and_2 (MemStore, Exec, Store);
  or or_1 (MemLoad, Fetch, and_1_out);
endmodule

module Registres (
  input  [2:0] SR1,
  input  [15:0] IN,
  input  [2:0] SR2,
  input  WriteReg,
  input  [2:0] DR_SR,
  output [15:0] R0,
  output [15:0] OUT_SR1,
  output [15:0] R1,
  output [15:0] R2,
  output [15:0] R3,
  output [15:0] OUT_SR2,
  output [15:0] R4,
  output [15:0] R5,
  output [15:0] OUT_SR,
  output [15:0] R6,
  output [15:0] R7
);

  wire decoder_1_out0, decoder_1_out1, decoder_1_out2, decoder_1_out3, decoder_1_out4, decoder_1_out5,
       decoder_1_out6, decoder_1_out7;

  Decoder #(.select(3), .disabled(0)) decoder_1 (
    .out0(decoder_1_out0), .out1(decoder_1_out1), .out2(decoder_1_out2), .out3(decoder_1_out3),
    .out4(decoder_1_out4), .out5(decoder_1_out5), .out6(decoder_1_out6), .out7(decoder_1_out7), .sel(DR_SR),
    .en(WriteReg));
  Register #(.width(16), .trigger("falling")) u_R0 (.D(IN), .Q(R0), .clk(decoder_1_out0));  // open: en, clr
  Register #(.width(16), .trigger("falling")) u_R1 (.D(IN), .Q(R1), .clk(decoder_1_out1));  // open: en, clr
  Register #(.width(16), .trigger("falling")) u_R2 (.D(IN), .Q(R2), .clk(decoder_1_out2));  // open: en, clr
  Register #(.width(16), .trigger("falling")) u_R3 (.D(IN), .Q(R3), .clk(decoder_1_out3));  // open: en, clr
  Register #(.width(16), .trigger("falling")) u_R4 (.D(IN), .Q(R4), .clk(decoder_1_out4));  // open: en, clr
  Register #(.width(16), .trigger("falling")) u_R5 (.D(IN), .Q(R5), .clk(decoder_1_out5));  // open: en, clr
  Register #(.width(16), .trigger("falling")) u_R6 (.D(IN), .Q(R6), .clk(decoder_1_out6));  // open: en, clr
  Register #(.width(16), .trigger("falling")) u_R7 (.D(IN), .Q(R7), .clk(decoder_1_out7));  // open: en, clr
  Multiplexer #(.select(3), .width(16), .enable("false")) multiplexer_1 (
    .in0(R0), .in1(R1), .in2(R2), .in3(R3), .in4(R4), .in5(R5), .in6(R6), .in7(R7), .out(OUT_SR1), .sel(SR1));
  Multiplexer #(.select(3), .width(16), .enable("false")) multiplexer_2 (
    .in0(R0), .in1(R1), .in2(R2), .in3(R3), .in4(R4), .in5(R5), .in6(R6), .in7(R7), .out(OUT_SR2), .sel(SR2));
  Multiplexer #(.select(3), .width(16), .enable("false")) multiplexer_3 (
    .in0(R0), .in1(R1), .in2(R2), .in3(R3), .in4(R4), .in5(R5), .in6(R6), .in7(R7), .out(OUT_SR), .sel(DR_SR));
endmodule

module RegPC (
  input  [15:0] IR,
  input  [15:0] R,
  input  H,
  input  Reset,
  input  Jump,
  input  TestNZP,
  output [15:0] PC
);

  wire and_1_out, and_2_out, and_3_out, not_1_out, or_1_out;
  wire [15:0] adder_1_out, adder_2_out, multiplexer_1_out, multiplexer_2_out, multiplexer_3_out,
       offset9_1_off9, offset11_1_sextoff11;

  Offset9 offset9_1 (.IR(IR), .Off9(offset9_1_off9));
  Offset11 offset11_1 (.IR(IR), .SEXTOff11(offset11_1_sextoff11));
  and and_1 (and_1_out, IR[14], Jump);
  and and_2 (and_2_out, Jump, TestNZP);
  Adder #(.width(16)) adder_1 (.a(PC), .b(16'h1), .out(adder_1_out));  // open: cin, cout
  Multiplexer #(.width(16), .disabled(0), .enable("false")) multiplexer_1 (
    .in0(offset9_1_off9), .in1(offset11_1_sextoff11), .out(multiplexer_1_out), .sel(and_1_out));
  not not_1 (not_1_out, IR[11]);
  or or_1 (or_1_out, and_1_out, and_2_out);
  Adder #(.width(16)) adder_2 (.a(adder_1_out), .b(multiplexer_1_out), .out(adder_2_out));  // open: cin, cout
  and and_3 (and_3_out, not_1_out, IR[14]);
  Multiplexer #(.width(16), .disabled(0), .enable("false")) multiplexer_2 (
    .in0(adder_2_out), .in1(R), .out(multiplexer_2_out), .sel(and_3_out));
  Multiplexer #(.width(16), .enable("false")) multiplexer_3 (
    .in0(adder_1_out), .in1(multiplexer_2_out), .out(multiplexer_3_out), .sel(or_1_out));
  Register #(.width(16), .trigger("falling")) u_PC (.D(multiplexer_3_out), .Q(PC), .clk(H), .clr(Reset));  // open: en

  // Notes on the sheet:
  //   BR : PC <- PC + SEXT(PCoffset9)
  //   JSR : PC <- PC+SEXT(PCoffset11)
  //   A COMPLETER v2
  //   JSR ssi JMP et 14
  //   pour BR
  //   pour JSR
  //   PC <- PC + 1
  //   BaseR
  //   BaseR ssi JMP ou JSRR
  //   A COMPLETER v2
  //   saut ssi JMP et (BR =>TestNZP)
  //   PC+Off
  //   pas saut
  //   saut
endmodule

module Offset11 (
  input  [15:0] IR,
  output [15:0] SEXTOff11
);

  assign SEXTOff11 = {{5{IR[10]}}, IR[10:0]};  // Bit_Extender bit_extender_1
endmodule

module WriteVal (
  input  Load,
  input  [15:0] ALURes,
  input  [15:0] MemOUT,
  input  [15:0] IR,
  input  [15:0] PC,
  output [15:0] RegIN
);

  wire JSR, LEA;
  wire [15:0] adder_1_out, adder_2_out, adder_3_out, offset9_1_off9;

  and and_1 (LEA, ~IR[12], IR[13], IR[14], IR[15]);  // AND_Gate
  and and_2 (JSR, ~IR[12], ~IR[13], IR[14], ~IR[15]);  // AND_Gate
  Adder #(.width(16)) adder_1 (.a(PC), .b(16'h1), .out(adder_1_out));  // open: cin, cout
  Adder #(.width(16)) adder_2 (.a(PC), .b(16'h1), .out(adder_2_out));  // open: cin, cout
  Offset9 offset9_1 (.IR(IR), .Off9(offset9_1_off9));
  Adder #(.width(16)) adder_3 (.a(offset9_1_off9), .b(adder_2_out), .out(adder_3_out));  // open: cin, cout
  Multiplexer #(.select(3), .width(16)) multiplexer_1 (
    .in0(ALURes), .in1(MemOUT), .in2(adder_3_out), .in3(adder_3_out), .in4(adder_1_out), .in5(adder_1_out),
    .in6(adder_1_out), .in7(adder_1_out), .out(RegIN), .sel({JSR, LEA, Load}));  // open: en

  // Notes on the sheet:
  //   RegIN = si JSR (100) alors PC (entrée 4)
  //   si LEA (010) alors PC+SEXT(Offset9) (entrée 2)
  //   si Load (001) alors MemOUT (entrée 1)
  //   ALURes (000) sinon
  //   RegIN = si JSR alors PC sinon si LEA alors PC+SEXT(Offset9) sinon si Load alors MemOUT sinon ALURes  
  //   MUX reçoit à l'entrée "select" les valeurs suivantes : 001 - Load, 010 - LEA, 100 - JSR ou 000
  //   On ajoute 1 chaque fois que LEA est exécutée 
  //   pour obtenir l'adresse de l'instruction suivante, c.a.d. PC
endmodule

module Scan (
  input  [15:0] IR,
  input  [15:0] IR_2,
  output [15:0] out_3
);

  wire and_2_out, and_3_out, and_4_out, and_5_out, and_6_out, and_7_out, and_8_out, and_9_out, and_10_out,
       and_11_out, and_12_out, and_13_out, and_14_out, and_15_out, and_16_out;

  and and_1 (out_3[15], IR[15], IR_2[15]);
  and and_2 (and_2_out, IR[14], IR_2[14]);
  and and_3 (and_3_out, IR[13], IR_2[13]);
  and and_4 (and_4_out, IR[12], IR_2[12]);
  and and_5 (and_5_out, IR[11], IR_2[11]);
  and and_6 (and_6_out, IR[10], IR_2[10]);
  and and_7 (and_7_out, IR[9], IR_2[9]);
  and and_8 (and_8_out, IR[8], IR_2[8]);
  and and_9 (and_9_out, IR[7], IR_2[7]);
  and and_10 (and_10_out, IR[6], IR_2[6]);
  and and_11 (and_11_out, IR[5], IR_2[5]);
  and and_12 (and_12_out, IR[4], IR_2[4]);
  and and_13 (and_13_out, IR[3], IR_2[3]);
  and and_14 (and_14_out, IR[2], IR_2[2]);
  and and_15 (and_15_out, IR[1], IR_2[1]);
  and and_16 (and_16_out, IR[0], IR_2[0]);
  xor xor_1 (out_3[14], out_3[15], and_2_out);
  xor xor_2 (out_3[13], out_3[14], and_3_out);
  xor xor_3 (out_3[12], out_3[13], and_4_out);
  xor xor_4 (out_3[11], out_3[12], and_5_out);
  xor xor_5 (out_3[10], out_3[11], and_6_out);
  xor xor_6 (out_3[9], out_3[10], and_7_out);
  xor xor_7 (out_3[8], out_3[9], and_8_out);
  xor xor_8 (out_3[7], out_3[8], and_9_out);
  xor xor_9 (out_3[6], out_3[7], and_10_out);
  xor xor_10 (out_3[5], out_3[6], and_11_out);
  xor xor_11 (out_3[4], out_3[5], and_12_out);
  xor xor_12 (out_3[3], out_3[4], and_13_out);
  xor xor_13 (out_3[2], out_3[3], and_14_out);
  xor xor_14 (out_3[1], out_3[2], and_15_out);
  xor xor_15 (out_3[0], out_3[1], and_16_out);

  // Notes on the sheet:
  //   première version du circuit de calcul pour SCAN
endmodule

module Scan_2 (
  input  [15:0] IR,
  input  [15:0] IR_2,
  output [15:0] out_3
);

  wire and_2_out, and_3_out, and_4_out, and_5_out, and_6_out, and_7_out, and_8_out, and_9_out, and_10_out,
       and_11_out, and_13_out, and_14_out, and_15_out, and_16_out, and_17_out, xor_2_out, xor_3_out,
       xor_4_out, xor_7_out, xor_8_out, xor_9_out, xor_10_out, xor_13_out, xor_16_out, xor_17_out, xor_20_out;

  and and_1 (out_3[15], IR[15], IR_2[15]);
  and and_2 (and_2_out, IR[14], IR_2[14]);
  and and_3 (and_3_out, IR[13], IR_2[13]);
  and and_4 (and_4_out, IR[12], IR_2[12]);
  and and_5 (and_5_out, IR[11], IR_2[11]);
  and and_6 (and_6_out, IR[10], IR_2[10]);
  and and_7 (and_7_out, IR[9], IR_2[9]);
  and and_8 (and_8_out, IR[8], IR_2[8]);
  and and_9 (and_9_out, IR[7], IR_2[7]);
  and and_10 (and_10_out, IR[6], IR_2[6]);
  and and_11 (and_11_out, IR[5], IR_2[5]);
  and and_12 (and_11_out, IR[5], IR_2[5]);
  and and_13 (and_13_out, IR[4], IR_2[4]);
  and and_14 (and_14_out, IR[3], IR_2[3]);
  and and_15 (and_15_out, IR[2], IR_2[2]);
  and and_16 (and_16_out, IR[1], IR_2[1]);
  and and_17 (and_17_out, IR[0], IR_2[0]);
  xor xor_1 (out_3[14], out_3[15], and_2_out);
  xor xor_2 (xor_2_out, and_3_out, and_4_out);
  xor xor_3 (xor_3_out, and_5_out, and_6_out);
  xor xor_4 (xor_4_out, and_7_out, and_8_out);
  xor xor_5 (out_3[13], out_3[14], and_3_out);
  xor xor_6 (out_3[12], out_3[14], xor_2_out);
  xor xor_7 (xor_7_out, and_9_out, and_10_out);
  xor xor_8 (xor_8_out, and_11_out, and_13_out);
  xor xor_9 (xor_9_out, and_14_out, and_15_out);
  xor xor_10 (xor_10_out, and_16_out, and_17_out);
  xor xor_11 (out_3[11], out_3[12], and_5_out);
  xor xor_12 (out_3[10], out_3[12], xor_3_out);
  xor xor_13 (xor_13_out, xor_3_out, xor_4_out);
  xor xor_14 (out_3[9], out_3[10], and_7_out);
  xor xor_15 (out_3[8], out_3[12], xor_13_out);
  xor xor_16 (xor_16_out, xor_7_out, xor_8_out);
  xor xor_17 (xor_17_out, xor_9_out, xor_10_out);
  xor xor_18 (out_3[7], out_3[8], and_9_out);
  xor xor_19 (out_3[6], out_3[8], xor_7_out);
  xor xor_20 (xor_20_out, xor_16_out, xor_17_out);
  xor xor_21 (out_3[5], out_3[6], and_11_out);
  xor xor_22 (out_3[4], out_3[6], xor_8_out);
  xor xor_23 (out_3[0], out_3[8], xor_20_out);
  xor xor_24 (out_3[3], out_3[4], and_14_out);
  xor xor_25 (out_3[2], out_3[4], xor_9_out);
  xor xor_26 (out_3[1], out_3[2], and_16_out);

  // Notes on the sheet:
  //   version optimisé du circuit de Calcul pour SCAN
  //   il permet d'eviter de faire beaucoup d'operation en cascade
  //   ce qui permet d'eviter de devoir faire (((a xor b) xor c) xor d)
  //   grace au fait qu'on peut decouper(a xor b xor c xor d) en (a xor b) xor(c xor d) 
endmodule

module choixDRSR_JSR (
  input  [15:0] IR,
  output [2:0] Output
);

  wire and_1_out, and_2_out, and_3_out, not_1_out, not_2_out, not_3_out;

  not not_1 (not_1_out, IR[12]);
  not not_2 (not_2_out, IR[13]);
  not not_3 (not_3_out, IR[15]);
  and and_1 (and_1_out, not_1_out, not_2_out);
  and and_2 (and_2_out, IR[14], not_3_out);
  Multiplexer #(.width(3), .enable("false")) multiplexer_1 (
    .in0(IR[11:9]), .in1(3'b111), .out(Output), .sel(and_3_out));
  and and_3 (and_3_out, and_1_out, and_2_out);
endmodule
