// Logisim project SCAN-opti.circ as structural Verilog: 1 circuit, main circuit main
module main (
  input  [15:0] IR,
  input  [15:0] in_2,
  input  [15:0] IR_2
);

  wire and_1_out, and_2_out, and_3_out, and_4_out, and_5_out, and_6_out, and_7_out, and_8_out, and_9_out,
       and_10_out, and_11_out, and_13_out, and_14_out, and_15_out, and_16_out, and_17_out, xor_1_out,
       xor_2_out, xor_3_out, xor_4_out, xor_5_out, xor_6_out, xor_7_out, xor_8_out, xor_9_out, xor_10_out,
       xor_11_out, xor_12_out, xor_13_out, xor_14_out, xor_15_out, xor_16_out, xor_17_out, xor_18_out,
       xor_19_out, xor_20_out, xor_21_out, xor_22_out, xor_23_out, xor_24_out, xor_25_out, xor_26_out;

  and and_1 (and_1_out, in_2[0], IR_2[0]);
  and and_2 (and_2_out, in_2[1], IR_2[1]);
  and and_3 (and_3_out, in_2[2], IR_2[2]);
  and and_4 (and_4_out, in_2[3], IR_2[3]);
  and and_5 (and_5_out, in_2[4], IR_2[4]);
  and and_6 (and_6_out, in_2[5], IR_2[5]);
  and and_7 (and_7_out, in_2[6], IR_2[6]);
  and and_8 (and_8_out, in_2[7], IR_2[7]);
  and and_9 (and_9_out, in_2[8], IR_2[8]);
  and and_10 (and_10_out, in_2[9], IR_2[9]);
  and and_11 (and_11_out, in_2[10], IR_2[10]);
  and and_12 (and_11_out, in_2[10], IR_2[10]);
  and and_13 (and_13_out, in_2[11], IR_2[11]);
  and and_14 (and_14_out, in_2[12], IR_2[12]);
  and and_15 (and_15_out, in_2[13], IR_2[13]);
  and and_16 (and_16_out, in_2[14], IR_2[14]);
  and and_17 (and_17_out, in_2[15], IR_2[15]);
  xor xor_1 (xor_1_out, and_1_out, and_2_out);
  xor xor_2 (xor_2_out, and_3_out, and_4_out);
  xor xor_3 (xor_3_out, and_5_out, and_6_out);
  xor xor_4 (xor_4_out, and_7_out, and_8_out);
  xor xor_5 (xor_5_out, xor_1_out, and_3_out);
  xor xor_6 (xor_6_out, xor_1_out, xor_2_out);
  xor xor_7 (xor_7_out, and_9_out, and_10_out);
  xor xor_8 (xor_8_out, and_11_out, and_13_out);
  xor xor_9 (xor_9_out, and_14_out, and_15_out);
  xor xor_10 (xor_10_out, and_16_out, and_17_out);
  xor xor_11 (xor_11_out, xor_6_out, and_5_out);
  xor xor_12 (xor_12_out, xor_6_out, xor_3_out);
  xor xor_13 (xor_13_out, xor_3_out, xor_4_out);
  xor xor_14 (xor_14_out, xor_12_out, and_7_out);
  xor xor_15 (xor_15_out, xor_6_out, xor_13_out);
  xor xor_16 (xor_16_out, xor_7_out, xor_8_out);
  xor xor_17 (xor_17_out, xor_9_out, xor_10_out);
  xor xor_18 (xor_18_out, xor_15_out, and_9_out);
  xor xor_19 (xor_19_out, xor_15_out, xor_7_out);
  xor xor_20 (xor_20_out, xor_16_out, xor_17_out);
  xor xor_21 (xor_21_out, xor_19_out, and_11_out);
  xor xor_22 (xor_22_out, xor_19_out, xor_8_out);
  xor xor_23 (xor_23_out, xor_15_out, xor_20_out);
  xor xor_24 (xor_24_out, xor_22_out, and_14_out);
  xor xor_25 (xor_25_out, xor_22_out, xor_9_out);
  xor xor_26 (xor_26_out, xor_25_out, and_16_out);

  assign IR = in_2;
endmodule
